// Logisim project circuito sequencial.circ as structural Verilog: 1 circuit, main circuit main
module main (
  input  Reset__R,
  input  set__S,
  output \Saída_Normal__Q ,
  output \Saída_complementar__C 
);

  nor nor_1 (\Saída_Normal__Q , Reset__R, \Saída_complementar__C );
  nor nor_2 (\Saída_complementar__C , set__S, \Saída_Normal__Q );
endmodule
