// Logisim project Circuito complemento de 2.circ as structural Verilog: 3 circuits, main circuit Somador completo 
module Somador_completo (
  input  in_1,
  input  A,
  input  B,
  output out_4,
  output out_5
);

  wire and_1_out, and_2_out, and_3_out, not_1_out, xor_1_out;

  not not_1 (not_1_out, A);
  and and_1 (and_1_out, not_1_out, B);
  and and_2 (and_2_out, in_1, not_1_out);
  and and_3 (and_3_out, B, in_1);
  xor xor_1 (xor_1_out, not_1_out, B);
  xor xor_2 (out_4, xor_1_out, in_1);
  or or_1 (out_5, and_1_out, and_2_out, and_3_out);
endmodule

module Meio_somador (
  input  A,
  input  B,
  output out_3,
  output out_4
);

  wire not_1_out;

  not not_1 (not_1_out, A);
  xor xor_1 (out_3, not_1_out, B);
  and and_1 (out_4, not_1_out, B);
endmodule

module complemento_de_2 (
  input  _4__Beats,
  input  _3__Beats,
  input  _2__Beats,
  input  _1__beats,
  input  C2,
  input  C1,
  output \_1__saída ,
  output \_2__saída ,
  output \_3__saída ,
  output \_4__saída ,
  output Overflow
);

  wire meio_somador_1_out_4, somador_completo_1_out_5, somador_completo_2_out_5;

  Meio_somador meio_somador_1 (.A(_1__beats), .B(C1), .out_3(\_1__saída ), .out_4(meio_somador_1_out_4));
  Somador_completo somador_completo_1 (
    .A(_2__Beats), .B(C2), .in_1(meio_somador_1_out_4), .out_4(\_2__saída ), .out_5(somador_completo_1_out_5));
  Somador_completo somador_completo_2 (
    .A(_3__Beats), .B(C2), .in_1(somador_completo_1_out_5), .out_4(\_3__saída ),
    .out_5(somador_completo_2_out_5));
  Somador_completo somador_completo_3 (
    .A(_4__Beats), .B(C2), .in_1(somador_completo_2_out_5), .out_4(\_4__saída ), .out_5(Overflow));

  // Notes on the sheet:
  //   OBS: O Meio Somador e o Somador Completo estão recebendo o A negado, e C1 esta com o beat  ligado no Meio Somador para representar a soma de 1 no complemento de 2. 
  //   Complemento de 2
endmodule
